// Logisim project haze.circ as structural Verilog: 5 circuits, main circuit main
module main (
  input  in_1
);

  wire aluoe, and_2_out, and_3_out, clk, clock_1_out, comparator_1_eq, dcdoe, execd, isrst, jmp, not_1_out,
       not_2_out, not_3_out, not_4_out, not_5_out, ramie, ramoe, rfrd1, rfrd2, rfwen;
  wire [1:0] op1, op2;
  wire [3:0] opcode;
  wire [7:0] alu_1_r, data, db_1_imm, rfo1, rfo2;
  wire [15:0] dbmem, pcacout, pcaout;

  Clock clock_1 (.out(clock_1_out));
  and and_1 (clk, execd, clock_1_out);
  and and_2 (and_2_out, jmp, comparator_1_eq);
  Comparator comparator_1 (.a({8{1'b0}}), .b(rfo2), .eq(comparator_1_eq));  // open: gt, lt
  not not_1 (not_1_out, and_2_out);
  not not_2 (not_2_out, clk);
  not not_3 (not_3_out, clk);
  db db_1 (.ain(pcaout), .mem(dbmem), .imm(db_1_imm), .op2(op2), .op1(op1), .opcode(opcode));
  rf rf_1 (
    .din(data), .ra1(op1), .wen(rfwen), .wa(op1), .ra2(op2), .clk(not_2_out), .rst(in_1), .out1(rfo1),
    .out2(rfo2));
  alu alu_1 (.opcode(opcode), .a(rfo1), .b(data), .r(alu_1_r));
  pc pc_1 (
    .jmp(and_2_out), .ai(dbmem), .en(not_1_out), .rst(in_1), .isrst(isrst), .clk(not_3_out), .ao(pcaout));  // open: iso
  assign data = dcdoe ? db_1_imm : 8'bz;  // Controlled_Buffer controlled_buffer_1
  assign data = rfrd1 ? rfo1 : 8'bz;  // Controlled_Buffer controlled_buffer_2
  assign data = rfrd2 ? rfo2 : 8'bz;  // Controlled_Buffer controlled_buffer_3
  assign data = aluoe ? alu_1_r : 8'bz;  // Controlled_Buffer controlled_buffer_4
  not not_4 (not_4_out, dbmem[15]);
  Hex_Digit_Display #(.decimalPoint("false")) hex_digit_display_1 (.value(pcacout[15:12]));
  Hex_Digit_Display #(.decimalPoint("false")) hex_digit_display_2 (.value(pcacout[11:8]));
  and and_3 (and_3_out, ramoe, not_4_out);
  RAM #(.addrWidth(15), .trigger("falling")) ram_1 (
    .addr(dbmem[14:0]), .we(ramie), .oe(and_3_out), .clk(not_5_out), .din(data), .dout(data));
  not not_5 (not_5_out, clk);
  Hex_Digit_Display #(.decimalPoint("false")) hex_digit_display_3 (.value(pcacout[7:4]));
  Hex_Digit_Display #(.decimalPoint("false")) hex_digit_display_4 (.value(pcacout[3:0]));
  // Probe on data

  // Other names for the same wires on the sheet: rst = in_1
endmodule

module db (
  input  [15:0] ain,
  output [15:0] mem,
  output [7:0] imm,
  output [1:0] op2,
  output [1:0] op1,
  output [3:0] opcode
);

  wire and_1_out, not_1_out;
  wire [7:0] rom_1_p2, rom_1_p3, rom_1_p4;

  not not_1 (not_1_out, ain[14]);
  // ROM #(.addrWidth(14), .line("quad")) rom_1: pin names not known; wires that end beside it: ain[13:0], rom_1_p2, rom_1_p3, rom_1_p4
  and and_1 (and_1_out, not_1_out, ain[15]);
  assign mem[7:0] = and_1_out ? rom_1_p2 : 8'bz;  // Controlled_Buffer controlled_buffer_1
  assign imm = and_1_out ? rom_1_p3 : 8'bz;  // Controlled_Buffer controlled_buffer_2
  assign {opcode, op1, op2} = and_1_out ? rom_1_p4 : 8'bz;  // Controlled_Buffer controlled_buffer_3

  assign mem[15:8] = imm;
endmodule

module pc (
  input  jmp,
  input  [15:0] ai,
  input  en,
  input  rst,
  input  isrst,
  input  clk,
  output [15:0] ao,
  output [2:0] iso
);

  wire and_1_out, counter_1_carry, not_1_out, or_1_out, or_2_out;
  wire [13:0] adder_1_out, multiplexer_1_out;

  Register #(.width(14)) register_1 (.D(multiplexer_1_out), .en(or_1_out), .clk(and_1_out), .Q(ao[13:0]), .clr(rst));
  Multiplexer #(.width(14)) multiplexer_1 (.in0(adder_1_out), .in1(ai[13:0]), .out(multiplexer_1_out), .sel(jmp));
  or or_1 (or_1_out, jmp, en);
  not not_1 (not_1_out, counter_1_carry);
  and and_1 (and_1_out, not_1_out, isrst);
  or or_2 (or_2_out, rst, jmp, isrst);
  Adder #(.width(14)) adder_1 (.a(ao[13:0]), .b(14'h3), .out(adder_1_out), .cin(1'b0));  // open: cout
  Counter #(.max('h7), .width(3)) counter_1 (
    .clr(or_2_out), .load(1'b0), .up(1'b1), .count(en), .clk(clk), .D(3'b000), .carry(counter_1_carry),
    .Q(iso));

  assign ao[15:14] = 2'b10;
endmodule

module alu (
  input  [3:0] opcode,
  input  [7:0] a,
  input  [7:0] b,
  output [7:0] r
);

  wire [7:0] adder_1_out, and_1_out, not_1_out, or_1_out, subtractor_1_out, xor_1_out;

  Adder adder_1 (.a(a), .b(b), .out(adder_1_out));  // open: cin, cout
  Subtractor subtractor_1 (.a(a), .b(b), .out(subtractor_1_out));  // open: bin, bout
  assign and_1_out = a & b;  // AND_Gate and_1, 8 bits wide
  assign or_1_out = a | b;  // OR_Gate or_1, 8 bits wide
  assign xor_1_out = a ^ b;  // XOR_Gate xor_1, 8 bits wide
  assign not_1_out = ~b;  // NOT_Gate not_1, 8 bits wide
  Multiplexer #(.select(4), .width(8)) multiplexer_1 (
    .in0({8{1'b0}}), .in1({8{1'b0}}), .in2({8{1'b0}}), .in3({8{1'b0}}), .in4(adder_1_out),
    .in5(subtractor_1_out), .in6(and_1_out), .in7(or_1_out), .in8(xor_1_out), .in9(not_1_out),
    .in10({8{1'b0}}), .in11({8{1'b0}}), .in12({8{1'b0}}), .in13({8{1'b0}}), .in14({8{1'b0}}),
    .in15({8{1'b0}}), .out(r), .sel(opcode));
endmodule

module rf (
  input  [7:0] din,
  input  [1:0] ra1,
  input  wen,
  input  [1:0] wa,
  input  [1:0] ra2,
  input  clk,
  input  rst,
  output [7:0] out1,
  output [7:0] out2
);

  wire decoder_1_out0, decoder_1_out1, decoder_1_out2, decoder_1_out3;
  wire [7:0] register_1_q, register_2_q, register_3_q, register_4_q;

  Decoder #(.select(2)) decoder_1 (
    .out0(decoder_1_out0), .out1(decoder_1_out1), .out2(decoder_1_out2), .out3(decoder_1_out3), .sel(wa),
    .en(wen));
  Register register_1 (.D(din), .en(decoder_1_out0), .clk(clk), .Q(register_1_q), .clr(rst));
  Register register_2 (.D(din), .en(decoder_1_out1), .clk(clk), .Q(register_2_q), .clr(rst));
  Register register_3 (.D(din), .en(decoder_1_out2), .clk(clk), .Q(register_3_q), .clr(rst));
  Register register_4 (.D(din), .en(decoder_1_out3), .clk(clk), .Q(register_4_q), .clr(rst));
  Multiplexer #(.select(2), .width(8)) multiplexer_1 (
    .in0(register_1_q), .in1(register_2_q), .in2(register_3_q), .in3(register_4_q), .out(out1), .sel(ra1));
  Multiplexer #(.select(2), .width(8)) multiplexer_2 (
    .in0(register_1_q), .in1(register_2_q), .in2(register_3_q), .in3(register_4_q), .out(out2), .sel(ra2));
endmodule
